// Logisim project nand2tetris.circ as structural Verilog: 2 circuits, main circuit main
module main (
  input  in_1,
  output out_2
);

  NotGate notgate_1 (.inp(in_1), .outp(out_2));
endmodule

module NotGate (
  input  inp,
  output outp
);

  nand nand_1 (outp, inp, inp);
endmodule
